# Fritzing sketch 02.potentiometer (saved by Fritzing 0.9.3b)
breadboards: 1

parts:
  Composant1 = Arduino MKR1000
  R1 = TRIMPOT [package=3362u-2]

nets:
  N1: Composant1.A0_DAC0, R1.WIPER
  N2: Composant1.GND, R1.CCW
  N3: Composant1.VCC, R1.CW

custom parts:
  Arduino MKR1000: MKR1000 is a powerful board that combines the functionality of the Zero and the Wi-Fi Shield. It is the ideal solution for makers wanting to design IoT projects with minimal previous experience in networking
