# Fritzing sketch 6_leds_potar (saved by Fritzing 0.9.3b)
circuit board: 6.88566cm x 5.36311cm
breadboards: 1

parts:
  R1 = Resistor [tolerance=±5% resistance=220 package=THT]
  LED1 = LED - 5mm [color="Red (633nm)" package="5 mm [THT]"]
  LED2 = LED - 5mm [color="Red (633nm)" package="5 mm [THT]"]
  LED3 = LED - 5mm [color="Green (555nm)" package="5 mm [THT]"]
  LED4 = LED - 5mm [color="Green (555nm)" package="5 mm [THT]"]
  LED5 = LED - 5mm [color="Yellow (595nm)" package="5 mm [THT]"]
  LED6 = LED - 5mm [color="Yellow (595nm)" package="5 mm [THT]"]
  R7 = Resistor [tolerance=±5% resistance=220 package=THT]
  R8 = Resistor [tolerance=±5% resistance=220 package=THT]
  R9 = Resistor [tolerance=±5% resistance=220 package=THT]
  R10 = Resistor [tolerance=±5% resistance=220 package=THT]
  R11 = Resistor [tolerance=±5% resistance=220 package=THT]
  R12 = TRIMPOT [package=3386u]
  Composant1 = Arduino MKR1000

nets:
  N1: R1.Pin_0, Composant1.14_TX
  N2: R1.Pin_1, LED1.anode
  N3: LED1.cathode, LED2.cathode, LED3.cathode, LED4.cathode, LED5.cathode, LED6.cathode, R12.CCW, R12.CW, Composant1.GND
  N4: LED2.anode, R7.Pin_1
  N5: LED3.anode, R8.Pin_1
  N6: LED4.anode, R9.Pin_1
  N7: LED5.anode, R10.Pin_1
  N8: LED6.anode, R11.Pin_1
  N9: R7.Pin_0, Composant1.D13_RX
  N10: R8.Pin_0, Composant1.D12_SCL
  N11: R9.Pin_0, Composant1.D11_SDA
  N12: R10.Pin_0, Composant1.D10_MISO
  N13: R11.Pin_0, Composant1.D9_SCK
  N14: R12.WIPER, Composant1.A0_DAC0

notes:
  CHASER_LIGHTS

custom parts:
  Arduino MKR1000: MKR1000 is a powerful board that combines the functionality of the Zero and the Wi-Fi Shield. It is the ideal solution for makers wanting to design IoT projects with minimal previous experience in networking

// code stored in the sketch: ChaserLights.ino
/*
  chaserlights
  
  This example is part of the Fritzing Creator Kit: www.fritzing.org/creator-kit.
*/

int pinsCount=8;                        // declaring the integer variable pinsCount
int pins[] = {2,3,4,5,6,7,8,9};          // declaring the array pins[]

void setup() {                
  for (int i=0; i<pinsCount; i=i+1){    // counting the variable i from 0 to 7
    pinMode(pins[i], OUTPUT);            // initialising the pin at index i of the array of pins as OUTPUT
  }
}

void loop() {
  for (int i=0; i<pinsCount; i=i+1){    // chasing right
    digitalWrite(pins[i], HIGH);         // switching the LED at index i on
    delay(100);                          // stopping the program for 100 milliseconds
    digitalWrite(pins[i], LOW);          // switching the LED at index i off
  }
  for (int i=pinsCount-1; i>0; i=i-1){   // chasing left (except the outer leds)
    digitalWrite(pins[i], HIGH);         // switching the LED at index i on
    delay(100);                          // stopping the program for 100 milliseconds
    digitalWrite(pins[i], LOW);          // switching the LED at index i off
  }
}
