# Fritzing sketch led (saved by Fritzing 0.9.3b)
breadboards: 1

parts:
  Composant1 = Arduino MKR1000
  LED1 = LED - 5mm [color="Red (633nm)" package="5 mm [THT]"]
  R2 = Resistor [tolerance=±5% resistance=220 package=THT]

nets:
  N1: Composant1.D10_MISO, LED1.anode
  N2: LED1.cathode, R2.Pin_1

custom parts:
  Arduino MKR1000: MKR1000 is a powerful board that combines the functionality of the Zero and the Wi-Fi Shield. It is the ideal solution for makers wanting to design IoT projects with minimal previous experience in networking
